# Fritzing sketch SmartSocketWiringDiagram (saved by Fritzing 0.9.3b)

parts:
  U1 = NodeMCU V3.0
  Part1 = RFID-RC522-v2
  KY-1 = Keyes Relay [package=THT]
  R2 = Resistor [tolerance=±5% resistance=1k package=THT]  # not connected
  R1 = Resistor [tolerance=±5% resistance=1k package=THT]  # not connected

nets:
  N1: U1.D1, Part1.RST
  N2: U1.D4, Part1.SDA
  3V3: U1.3V3, Part1.3.3V
  GND: U1.GND, Part1.GND, KY-1.ground
  N3: U1.D5, Part1.SCK
  N4: U1.D6, Part1.MISO
  N5: U1.D7, Part1.MOSI
  N6: U1.D8, KY-1.power
  N7: U1.Vin, KY-1.signal

custom parts:
  NodeMCU V3.0: ESP8266 based NodeMCU
  RFID-RC522-v2: A simple China made RFID-RC522 Reader; do check the pin labels, as this is a MFRC522 based clone.
  Keyes Relay: The Keyes 5V relay module is suitable for SCM development, home appliance control. It uses a 5V~12V TIL control signal which can control DC / AC signal.
